// Logisim project P0_L0_CRC.circ as structural Verilog: 2 circuits, main circuit CRC
module CRC (
  input  [7:0] in_1,
  input  [3:0] in_2,
  output [10:0] Output
);

  wire [2:0] n4bit_mod2_1_remainder, n4bit_mod2_2_remainder, n4bit_mod2_3_remainder, n4bit_mod2_5_remainder,
       n4bit_mod2_6_remainder, n4bit_mod2_7_remainder, remainder;

  _4Bit_Mod2 u_4bit_mod2_1 (
    .in_1(in_1[2]), .in_2(n4bit_mod2_2_remainder), .in_3(in_2), .remainder(n4bit_mod2_1_remainder));
  _4Bit_Mod2 u_4bit_mod2_2 (.in_1(in_1[3]), .in_2(remainder), .in_3(in_2), .remainder(n4bit_mod2_2_remainder));
  _4Bit_Mod2 u_4bit_mod2_3 (
    .in_1(in_1[1]), .in_2(n4bit_mod2_1_remainder), .in_3(in_2), .remainder(n4bit_mod2_3_remainder));
  _4Bit_Mod2 u_4bit_mod2_4 (.in_1(in_1[4]), .in_2(in_1[7:5]), .in_3(in_2), .remainder(remainder));
  _4Bit_Mod2 u_4bit_mod2_5 (
    .in_1(in_1[0]), .in_2(n4bit_mod2_3_remainder), .in_3(in_2), .remainder(n4bit_mod2_5_remainder));
  _4Bit_Mod2 u_4bit_mod2_6 (
    .in_1(1'b0), .in_2(n4bit_mod2_5_remainder), .in_3(in_2), .remainder(n4bit_mod2_6_remainder));
  _4Bit_Mod2 u_4bit_mod2_7 (
    .in_1(1'b0), .in_2(n4bit_mod2_6_remainder), .in_3(in_2), .remainder(n4bit_mod2_7_remainder));
  _4Bit_Mod2 u_4bit_mod2_8 (.in_1(1'b0), .in_2(n4bit_mod2_7_remainder), .in_3(in_2), .remainder(Output[2:0]));

  assign Output[10:3] = in_1;

  // Other names for the same wires on the sheet: divisor[3:0] = in_2; remainder_final[2:0] = Output[2:0];
  //   dividend[7:0] = in_1; implement[6:3] = in_1[3:0]; origin[3:0] = in_1[7:4]
endmodule

module _4Bit_Mod2 (
  input  in_1,
  input  [2:0] in_2,
  input  [3:0] in_3,
  output [2:0] remainder
);

  wire [3:0] xor_1_out;
  wire [3:3] multiplexer_1_out;

  assign xor_1_out = in_3 ^ {in_2, in_1};  // XOR_Gate xor_1, 4 bits wide
  Multiplexer #(.width(4)) multiplexer_1 (
    .in0({in_2, in_1}), .in1(xor_1_out), .out({multiplexer_1_out[3], remainder}), .sel(in_2[2]));  // open: en

  // Other names for the same wires on the sheet: dividend[3:0] = {in_2, in_1}; divisor[3:0] = in_3
endmodule
