// Logisim project P0_L0_FSM.circ as structural Verilog: 4 circuits, main circuit fsm
module register (
  input  in_1,
  input  in_2,
  input  in_3,
  input  in_4,
  input  in_5,
  output out_6,
  output out_7,
  output out_8
);

  wire and_1_out, and_2_out, and_3_out, not_1_out;

  not not_1 (not_1_out, in_1);
  and and_1 (and_1_out, not_1_out, in_2);
  and and_2 (and_2_out, not_1_out, in_3);
  and and_3 (and_3_out, not_1_out, in_4);
  Register #(.width(1)) register_1 (.D(and_1_out), .Q(out_6), .clk(in_5));  // open: en, clr
  Register #(.width(1)) register_2 (.D(and_2_out), .Q(out_7), .clk(in_5));  // open: en, clr
  Register #(.width(1)) register_3 (.D(and_3_out), .Q(out_8), .clk(in_5));  // open: en, clr
endmodule

module trans (
  input  pre1,
  input  pre2,
  input  pre3,
  input  char1,
  input  char2,
  output s1,
  output s2,
  output s3
);

  wire and_1_out, and_2_out, and_3_out, and_4_out, and_5_out, and_6_out, and_7_out, and_8_out, and_9_out,
       and_10_out, and_11_out, and_12_out, and_13_out, and_14_out, and_15_out, and_16_out, and_17_out,
       and_18_out, and_19_out, and_20_out, and_21_out, and_22_out, and_23_out, and_24_out, and_25_out,
       and_26_out, and_27_out, and_28_out, and_29_out, and_30_out, and_31_out, and_32_out, not_1_out,
       not_2_out, not_3_out, not_4_out, not_5_out, not_6_out, not_7_out, not_8_out, not_9_out, not_10_out,
       not_11_out, not_12_out, not_13_out, not_14_out, not_15_out, not_16_out, not_17_out, not_18_out,
       not_19_out, not_20_out, not_21_out, not_22_out, not_23_out, not_24_out, not_25_out, not_26_out,
       not_27_out, not_28_out, or_2_out, or_3_out, or_4_out, or_5_out, or_6_out;

  not not_1 (not_1_out, pre1);
  not not_2 (not_2_out, pre2);
  not not_3 (not_3_out, pre3);
  not not_4 (not_4_out, char2);
  not not_5 (not_5_out, pre1);
  not not_6 (not_6_out, pre2);
  not not_7 (not_7_out, pre3);
  not not_8 (not_8_out, char1);
  not not_9 (not_9_out, pre1);
  and and_1 (and_1_out, not_1_out, pre2);
  not not_10 (not_10_out, char2);
  and and_2 (and_2_out, pre1, not_2_out);
  and and_3 (and_3_out, not_3_out, not_4_out);
  not not_11 (not_11_out, pre1);
  not not_12 (not_12_out, pre2);
  not not_13 (not_13_out, char1);
  not not_14 (not_14_out, pre1);
  not not_15 (not_15_out, pre2);
  not not_16 (not_16_out, char2);
  and and_4 (and_4_out, not_5_out, pre2);
  not not_17 (not_17_out, pre3);
  not not_18 (not_18_out, char1);
  not not_19 (not_19_out, pre2);
  not not_20 (not_20_out, pre3);
  not not_21 (not_21_out, char2);
  and and_5 (and_5_out, not_6_out, not_7_out);
  and and_6 (and_6_out, not_8_out, char2);
  and and_7 (and_7_out, not_9_out, pre3);
  not not_22 (not_22_out, char2);
  not not_23 (not_23_out, pre1);
  not not_24 (not_24_out, char1);
  not not_25 (not_25_out, pre2);
  not not_26 (not_26_out, char1);
  not not_27 (not_27_out, pre3);
  not not_28 (not_28_out, char1);
  and and_8 (and_8_out, and_1_out, not_10_out);
  or or_1 (s1, and_8_out, and_9_out);
  and and_9 (and_9_out, and_2_out, and_3_out);
  and and_10 (and_10_out, not_11_out, not_12_out);
  and and_11 (and_11_out, and_10_out, and_12_out);
  and and_12 (and_12_out, pre3, not_13_out);
  and and_13 (and_13_out, not_14_out, not_15_out);
  and and_14 (and_14_out, and_13_out, and_15_out);
  and and_15 (and_15_out, pre3, not_16_out);
  and and_16 (and_16_out, and_4_out, not_17_out);
  and and_17 (and_17_out, and_16_out, and_18_out);
  and and_18 (and_18_out, not_18_out, char2);
  and and_19 (and_19_out, pre1, not_19_out);
  and and_20 (and_20_out, and_19_out, and_21_out);
  and and_21 (and_21_out, not_20_out, not_21_out);
  and and_22 (and_22_out, and_5_out, and_6_out);
  or or_2 (or_2_out, and_22_out, and_23_out);
  and and_23 (and_23_out, and_7_out, not_22_out);
  and and_24 (and_24_out, not_23_out, pre2);
  and and_25 (and_25_out, and_24_out, and_26_out);
  and and_26 (and_26_out, pre3, not_24_out);
  and and_27 (and_27_out, pre1, not_25_out);
  and and_28 (and_28_out, and_27_out, and_29_out);
  and and_29 (and_29_out, not_26_out, char2);
  and and_30 (and_30_out, pre1, not_27_out);
  and and_31 (and_31_out, and_30_out, and_32_out);
  and and_32 (and_32_out, not_28_out, char2);
  or or_3 (or_3_out, and_11_out, and_14_out);
  or or_4 (or_4_out, and_17_out, and_20_out);
  or or_5 (or_5_out, or_2_out, and_25_out);
  or or_6 (or_6_out, and_28_out, and_31_out);
  or or_7 (s2, or_3_out, or_4_out);
  or or_8 (s3, or_5_out, or_6_out);
endmodule

module \output  (
  input  s1,
  input  s2,
  input  s3,
  input  op1,
  input  op2,
  output out_6
);

  wire and_1_out, and_2_out, and_3_out, and_4_out, comparator_1_eq, not_1_out, not_2_out, not_3_out;

  not not_1 (not_1_out, s1);
  not not_2 (not_2_out, s2);
  not not_3 (not_3_out, s3);
  Comparator #(.width(1)) comparator_1 (.a(op2), .b(1'b0), .eq(comparator_1_eq));  // open: gt, lt
  and and_1 (and_1_out, not_1_out, s2, s3);
  and and_2 (and_2_out, s1, not_2_out, not_3_out);
  and and_3 (and_3_out, comparator_1_eq, and_1_out);
  and and_4 (and_4_out, and_2_out, comparator_1_eq);
  or or_1 (out_6, and_3_out, and_4_out);
endmodule

module fsm (
  input  in_1,
  input  [1:0] in_2,
  output out_3
);

  wire clock_1_out, register_1_out_6, register_1_out_7, register_1_out_8, trans_1_s1, trans_1_s2, trans_1_s3;

  Clock clock_1 (.out(clock_1_out));
  trans trans_1 (
    .pre1(register_1_out_6), .pre2(register_1_out_7), .pre3(register_1_out_8), .char1(in_2[1]),
    .char2(in_2[0]), .s1(trans_1_s1), .s2(trans_1_s2), .s3(trans_1_s3));
  register register_1 (
    .in_1(in_1), .in_2(trans_1_s1), .in_3(trans_1_s2), .in_4(trans_1_s3), .in_5(clock_1_out),
    .out_6(register_1_out_6), .out_7(register_1_out_7), .out_8(register_1_out_8));
  \output  output_1 (
    .s1(register_1_out_6), .s2(register_1_out_7), .s3(register_1_out_8), .op1(in_2[1]), .op2(in_2[0]),
    .out_6(out_3));
endmodule
