// Logisim project P0_L0_GRF.circ as structural Verilog: 2 circuits, main circuit grf
module grf (
  input  clk,
  input  reset,
  input  WE,
  input  [4:0] A1,
  input  [4:0] A2,
  input  [4:0] A3,
  input  [31:0] WD,
  output [31:0] RD1,
  output [31:0] RD2
);

  wire [31:0] _1, _2, _3, _4, _5, _6, _7, _8, _9, _10, _11, _12, _13, _14, _15, _16, _17, _18, _19, _20, _21,
       _22, _23, _24, _25, _26, _27, _28, _29, _30, _31, _32, demultiplexer_1_out0, demultiplexer_1_out1,
       demultiplexer_1_out2, demultiplexer_1_out3, demultiplexer_1_out4, demultiplexer_1_out5,
       demultiplexer_1_out6, demultiplexer_1_out7, demultiplexer_1_out8, demultiplexer_1_out9,
       demultiplexer_1_out10, demultiplexer_1_out11, demultiplexer_1_out12, demultiplexer_1_out13,
       demultiplexer_1_out14, demultiplexer_1_out15, demultiplexer_1_out16, demultiplexer_1_out17,
       demultiplexer_1_out18, demultiplexer_1_out19, demultiplexer_1_out20, demultiplexer_1_out21,
       demultiplexer_1_out22, demultiplexer_1_out23, demultiplexer_1_out24, demultiplexer_1_out25,
       demultiplexer_1_out26, demultiplexer_1_out27, demultiplexer_1_out28, demultiplexer_1_out29,
       demultiplexer_1_out30, demultiplexer_1_out31;

  Demultiplexer #(.select(5), .width(32), .tristate("true")) demultiplexer_1 (
    .out0(demultiplexer_1_out0), .out1(demultiplexer_1_out1), .out2(demultiplexer_1_out2),
    .out3(demultiplexer_1_out3), .out4(demultiplexer_1_out4), .out5(demultiplexer_1_out5),
    .out6(demultiplexer_1_out6), .out7(demultiplexer_1_out7), .out8(demultiplexer_1_out8),
    .out9(demultiplexer_1_out9), .out10(demultiplexer_1_out10), .out11(demultiplexer_1_out11),
    .out12(demultiplexer_1_out12), .out13(demultiplexer_1_out13), .out14(demultiplexer_1_out14),
    .out15(demultiplexer_1_out15), .out16(demultiplexer_1_out16), .out17(demultiplexer_1_out17),
    .out18(demultiplexer_1_out18), .out19(demultiplexer_1_out19), .out20(demultiplexer_1_out20),
    .out21(demultiplexer_1_out21), .out22(demultiplexer_1_out22), .out23(demultiplexer_1_out23),
    .out24(demultiplexer_1_out24), .out25(demultiplexer_1_out25), .out26(demultiplexer_1_out26),
    .out27(demultiplexer_1_out27), .out28(demultiplexer_1_out28), .out29(demultiplexer_1_out29),
    .out30(demultiplexer_1_out30), .out31(demultiplexer_1_out31), .in(WD), .sel(A3), .en(WE));
  register register_1 (.in_1(demultiplexer_1_out0), .in_2(WE), .in_3(clk), .in_4(1'b1), .out_5(_1));
  register register_2 (.in_1(demultiplexer_1_out1), .in_2(WE), .in_3(clk), .in_4(reset), .out_5(_2));
  Multiplexer #(.select(5), .width(32)) multiplexer_1 (
    .in0(_1), .in1(_2), .in2(_3), .in3(_4), .in4(_5), .in5(_6), .in6(_7), .in7(_8), .in8(_9), .in9(_10),
    .in10(_11), .in11(_12), .in12(_13), .in13(_14), .in14(_15), .in15(_16), .in16(_17), .in17(_18),
    .in18(_19), .in19(_20), .in20(_21), .in21(_22), .in22(_23), .in23(_24), .in24(_25), .in25(_26),
    .in26(_27), .in27(_28), .in28(_29), .in29(_30), .in30(_31), .in31(_32), .out(RD1), .sel(A1));  // open: en
  register register_3 (.in_1(demultiplexer_1_out2), .in_2(WE), .in_3(clk), .in_4(reset), .out_5(_3));
  register register_4 (.in_1(demultiplexer_1_out3), .in_2(WE), .in_3(clk), .in_4(reset), .out_5(_4));
  register register_5 (.in_1(demultiplexer_1_out4), .in_2(WE), .in_3(clk), .in_4(reset), .out_5(_5));
  register register_6 (.in_1(demultiplexer_1_out5), .in_2(WE), .in_3(clk), .in_4(reset), .out_5(_6));
  register register_7 (.in_1(demultiplexer_1_out6), .in_2(WE), .in_3(clk), .in_4(reset), .out_5(_7));
  register register_8 (.in_1(demultiplexer_1_out7), .in_2(WE), .in_3(clk), .in_4(reset), .out_5(_8));
  register register_9 (.in_1(demultiplexer_1_out8), .in_2(WE), .in_3(clk), .in_4(reset), .out_5(_9));
  register register_10 (.in_1(demultiplexer_1_out9), .in_2(WE), .in_3(clk), .in_4(reset), .out_5(_10));
  register register_11 (.in_1(demultiplexer_1_out10), .in_2(WE), .in_3(clk), .in_4(reset), .out_5(_11));
  register register_12 (.in_1(demultiplexer_1_out11), .in_2(WE), .in_3(clk), .in_4(reset), .out_5(_12));
  register register_13 (.in_1(demultiplexer_1_out12), .in_2(WE), .in_3(clk), .in_4(reset), .out_5(_13));
  register register_14 (.in_1(demultiplexer_1_out13), .in_2(WE), .in_3(clk), .in_4(reset), .out_5(_14));
  Multiplexer #(.select(5), .width(32)) multiplexer_2 (
    .in0(_1), .in1(_2), .in2(_3), .in3(_4), .in4(_5), .in5(_6), .in6(_7), .in7(_8), .in8(_9), .in9(_10),
    .in10(_11), .in11(_12), .in12(_13), .in13(_14), .in14(_15), .in15(_16), .in16(_17), .in17(_18),
    .in18(_19), .in19(_20), .in20(_21), .in21(_22), .in22(_23), .in23(_24), .in24(_25), .in25(_26),
    .in26(_27), .in27(_28), .in28(_29), .in29(_30), .in30(_31), .in31(_32), .out(RD2), .sel(A2));  // open: en
  register register_15 (.in_1(demultiplexer_1_out14), .in_2(WE), .in_3(clk), .in_4(reset), .out_5(_15));
  register register_16 (.in_1(demultiplexer_1_out15), .in_2(WE), .in_3(clk), .in_4(reset), .out_5(_16));
  register register_17 (.in_1(demultiplexer_1_out16), .in_2(WE), .in_3(clk), .in_4(reset), .out_5(_17));
  register register_18 (.in_1(demultiplexer_1_out17), .in_2(WE), .in_3(clk), .in_4(reset), .out_5(_18));
  register register_19 (.in_1(demultiplexer_1_out18), .in_2(WE), .in_3(clk), .in_4(reset), .out_5(_19));
  register register_20 (.in_1(demultiplexer_1_out19), .in_2(WE), .in_3(clk), .in_4(reset), .out_5(_20));
  register register_21 (.in_1(demultiplexer_1_out20), .in_2(WE), .in_3(clk), .in_4(reset), .out_5(_21));
  register register_22 (.in_1(demultiplexer_1_out21), .in_2(WE), .in_3(clk), .in_4(reset), .out_5(_22));
  register register_23 (.in_1(demultiplexer_1_out22), .in_2(WE), .in_3(clk), .in_4(reset), .out_5(_23));
  register register_24 (.in_1(demultiplexer_1_out23), .in_2(WE), .in_3(clk), .in_4(reset), .out_5(_24));
  register register_25 (.in_1(demultiplexer_1_out24), .in_2(WE), .in_3(clk), .in_4(reset), .out_5(_25));
  register register_26 (.in_1(demultiplexer_1_out25), .in_2(WE), .in_3(clk), .in_4(reset), .out_5(_26));
  register register_27 (.in_1(demultiplexer_1_out26), .in_2(WE), .in_3(clk), .in_4(reset), .out_5(_27));
  register register_28 (.in_1(demultiplexer_1_out27), .in_2(WE), .in_3(clk), .in_4(reset), .out_5(_28));
  register register_29 (.in_1(demultiplexer_1_out28), .in_2(WE), .in_3(clk), .in_4(reset), .out_5(_29));
  register register_30 (.in_1(demultiplexer_1_out29), .in_2(WE), .in_3(clk), .in_4(reset), .out_5(_30));
  register register_31 (.in_1(demultiplexer_1_out30), .in_2(WE), .in_3(clk), .in_4(reset), .out_5(_31));
  register register_32 (.in_1(demultiplexer_1_out31), .in_2(WE), .in_3(clk), .in_4(reset), .out_5(_32));
endmodule

module register (
  input  [31:0] in_1,
  input  in_2,
  input  in_3,
  input  in_4,
  output [31:0] out_5
);

  Register #(.width(32)) register_1 (.D(in_1), .en(in_2), .Q(out_5), .clk(in_3), .clr(in_4));
endmodule
