// Logisim project P0_L1_FTOI.circ as structural Verilog: 1 circuit, main circuit ftoi
module ftoi (
  input  [15:0] Input,
  output [31:0] out_2
);

  wire comparator_1_lt, comparator_2_eq, or_1_out;
  wire [4:0] subtractor_1_out;
  wire [31:0] multiplexer_1_out, negator_1_out, shifter_1_out;

  Subtractor #(.width(5)) subtractor_1 (.a(Input[14:10]), .b(5'b01111), .out(subtractor_1_out));  // open: bin, bout
  Comparator #(.width(5), .mode("unsigned")) comparator_1 (
    .a(Input[14:10]), .b(5'b01111), .lt(comparator_1_lt));  // open: gt, eq
  Comparator #(.width(5)) comparator_2 (.a(Input[14:10]), .b({5{1'b1}}), .eq(comparator_2_eq));  // open: gt, lt
  Shifter #(.width(32)) shifter_1 (.in({22'h1, Input[9:0]}), .\dist (subtractor_1_out), .out(shifter_1_out));
  or or_1 (or_1_out, comparator_1_lt, comparator_2_eq);
  Multiplexer #(.width(32)) multiplexer_1 (
    .in0({{10{1'b0}}, shifter_1_out[31:10]}), .in1(negator_1_out), .out(multiplexer_1_out), .sel(Input[15]));  // open: en
  Negator #(.width(32)) negator_1 (.in({{10{1'b0}}, shifter_1_out[31:10]}), .out(negator_1_out));
  Multiplexer #(.width(32)) multiplexer_2 (
    .in0(multiplexer_1_out), .in1({32{1'b0}}), .out(out_2), .sel(or_1_out));  // open: en
endmodule
