// Logisim project P4_L0_weak_2023_DEBUG.circ as structural Verilog: 8 circuits, main circuit main
module main (
  input  reset,
  output [31:0] out_2,
  output [31:0] out_3,
  output out_4,
  output [4:0] out_5,
  output [31:0] out_6,
  output out_7,
  output [31:0] out_8,
  output [31:0] out_9
);

  wire alu_1_equal, ALUSrc, and_1_out, Branch, clk, isByte, issigned_extend, MemtoReg, RegDst;
  wire [2:0] ALUCtrl;
  wire [23:0] MemAddr, shifter_1_out;
  wire [31:0] alu_1_alu_result, dm_1_wd1, ext_1_out, grf_1_rd1, multiplexer_2_out, npc_1_next, PC;

  Clock clock_1 (.out(clk));
  IFU ifu_1 (.Next(npc_1_next), .Instr(out_2), .Now(PC), .clk(clk), .reset(reset));
  NPC npc_1 (
    .Now(PC), .Extender(ext_1_out), .Next(npc_1_next), .ins_26(out_2[25:0]), .ra(grf_1_rd1), .Equal(and_1_out));
  Controller controller_1 (
    .Funct(out_2[5:0]), .Opcode(out_2[31:26]), .MemtoReg(MemtoReg), .MemWrite(out_7), .Branch(Branch),
    .ALU_op(ALUCtrl), .ALUSrc(ALUSrc), .RegDst(RegDst), .RegWrite(out_4), .Extop(issigned_extend),
    .isByte(isByte));
  Multiplexer #(.width(5)) multiplexer_1 (
    .in0(out_2[20:16]), .in1(out_2[15:11]), .out(out_5), .sel(RegDst));  // open: en
  EXT ext_1 (.init_imm(out_2[15:0]), .Out(ext_1_out), .ext_sign(issigned_extend));
  GRF grf_1 (
    .A1(out_2[25:21]), .A2(out_2[20:16]), .A3(out_5), .WD(out_6), .clk(clk), .reset(reset), .WE(out_4),
    .RD1(grf_1_rd1), .RD2(out_9));
  Multiplexer #(.width(32)) multiplexer_2 (
    .in0(out_9), .in1(ext_1_out), .out(multiplexer_2_out), .sel(ALUSrc));  // open: en
  ALU alu_1 (
    .Src1(grf_1_rd1), .Src2(multiplexer_2_out), .Equal(alu_1_equal),
    .ALU_result({alu_1_alu_result[31:26], MemAddr, alu_1_alu_result[1:0]}), .ALU_OP(ALUCtrl));
  // Probe on {alu_1_alu_result[31:26], MemAddr, alu_1_alu_result[1:0]}
  // Probe on out_9
  and and_1 (and_1_out, Branch, alu_1_equal);
  DM dm_1 (
    .Addr({alu_1_alu_result[31:26], MemAddr, alu_1_alu_result[1:0]}), .Data(out_9), .isByte(isByte),
    .Memwrite(out_7), .clk(clk), .reset(reset), .WD1(dm_1_wd1));
  // Probe on dm_1_wd1
  Multiplexer #(.width(32)) multiplexer_3 (
    .in0({alu_1_alu_result[31:26], MemAddr, alu_1_alu_result[1:0]}), .in1(dm_1_wd1), .out(out_6),
    .sel(MemtoReg));  // open: en
  Adder #(.width(32)) adder_1 (.a(PC), .b(32'h3000), .out(out_3));  // open: cin, cout
  Shifter #(.width(24)) shifter_1 (.in(MemAddr), .\dist (5'b00010), .out(shifter_1_out));
  assign out_8 = {{8{1'b0}}, shifter_1_out};  // Bit_Extender bit_extender_1

  // Other names for the same wires on the sheet: instr[31:0] = out_2; MemData[31:0] = out_9; memWrite = out_7;
  //   RegAddr[4:0] = out_5; RegWrite = out_4; RegData[31:0] = out_6; WD[31:0] = out_6
endmodule

module IFU (
  input  [31:0] Next,
  input  clk,
  input  reset,
  output [31:0] Instr,
  output [31:0] Now
);

  Register #(.width(32)) PC (.D(Next), .Q(Now), .clk(clk), .clr(reset));  // open: en
  ROM #(.addrWidth(24), .dataWidth(32)) rom_1 (.addr(Now[25:2]), .data(Instr));  // open: sel

  // Notes on the sheet:
  //   IM
  //   contents of rom_1 (hex, n*v repeats v):
  //   3404007b 348501c8 3c06007b 3c07ffff 34e7ffff 868020 878820 e79020 34080000 ad040000 ad050004
  //   ad060008 ad07000c ad100010 ad110014 ad120018 8d040000 8d05000c ad04001c ad050020 34040001 34050002
  //   34060001 10850001 10860001 ad040024 ad050028
endmodule

module NPC (
  input  [31:0] Now,
  input  [31:0] Extender,
  input  Equal,
  input  [25:0] ins_26,
  input  [31:0] ra,
  output [31:0] Next
);

  wire [2:0] undriven;
  wire [31:0] PC_4, PC_4_offset, shifter_1_out;

  Shifter #(.width(32)) shifter_1 (.in(Extender), .\dist (5'b00010), .out(shifter_1_out));
  Adder #(.width(32)) adder_1 (.a(Now), .b(32'h4), .out(PC_4));  // open: cin, cout
  Multiplexer #(.select(3), .width(32)) multiplexer_1 (
    .in0(PC_4), .in1(PC_4_offset), .in2({Now[31:28], ins_26, 2'b00}), .in3(ra), .out(Next), .sel(undriven));  // open: in4, in5, in6, in7, en
  Adder #(.width(32)) adder_2 (.a(PC_4), .b(shifter_1_out), .out(PC_4_offset));  // open: cin, cout

  // Other names for the same wires on the sheet: ins_26_ext[31:2] = {Now[31:28], ins_26}
endmodule

module ALU (
  input  [31:0] Src1,
  input  [31:0] Src2,
  input  [2:0] ALU_OP,
  output Equal,
  output [31:0] ALU_result
);

  wire [31:0] adder_1_out, or_1_out, subtractor_1_out;

  Subtractor #(.width(32)) subtractor_1 (.a(Src1), .b(Src2), .out(subtractor_1_out));  // open: bin, bout
  Adder #(.width(32)) adder_1 (.a(Src1), .b(Src2), .out(adder_1_out));  // open: cin, cout
  Comparator #(.width(32)) comparator_1 (.a(Src1), .b(Src2), .eq(Equal));  // open: gt, lt
  assign or_1_out = Src1 | Src2;  // OR_Gate or_1, 32 bits wide
  Multiplexer #(.select(3), .width(32)) multiplexer_1 (
    .in0(subtractor_1_out), .in1(adder_1_out), .in2(or_1_out), .in3({Src2[15:0], {16{1'b0}}}),
    .out(ALU_result), .sel(ALU_OP));  // open: in4, in5, in6, in7, en
endmodule

module GRF (
  input  [4:0] A1,
  input  [4:0] A2,
  input  [4:0] A3,
  input  [31:0] WD,
  input  clk,
  input  reset,
  input  WE,
  output [31:0] RD1,
  output [31:0] RD2
);

  wire [31:0] in1, in2, in3, in4, in5, in6, in7, in8, in9, in10, in11, in12, in13, in14, in15, in16, in17,
       in18, in19, in20, in21, in22, in23, in24, in25, in26, in27, in28, in29, in30, in31, register_1_q,
       register_2_q, register_3_q, register_4_q, register_5_q, register_6_q, register_7_q, register_8_q,
       register_9_q, register_10_q, register_11_q, register_12_q, register_13_q, register_14_q,
       register_15_q, register_16_q, register_17_q, register_18_q, register_19_q, register_20_q,
       register_21_q, register_22_q, register_23_q, register_24_q, register_25_q, register_26_q,
       register_27_q, register_28_q, register_29_q, register_30_q, register_31_q, register_32_q;

  Register #(.width(32)) register_1 (.D({32{1'b0}}), .en(WE), .Q(register_1_q), .clk(clk), .clr(reset));
  Register #(.width(32)) register_2 (.D(in8), .en(WE), .Q(register_2_q), .clk(clk), .clr(reset));
  Register #(.width(32)) register_3 (.D(in16), .en(WE), .Q(register_3_q), .clk(clk), .clr(reset));
  Register #(.width(32)) register_4 (.D(in24), .en(WE), .Q(register_4_q), .clk(clk), .clr(reset));
  Multiplexer #(.select(5), .width(32)) multiplexer_1 (
    .in0(register_1_q), .in1(register_5_q), .in2(register_9_q), .in3(register_13_q), .in4(register_17_q),
    .in5(register_21_q), .in6(register_25_q), .in7(register_29_q), .in8(register_2_q), .in9(register_6_q),
    .in10(register_10_q), .in11(register_14_q), .in12(register_18_q), .in13(register_22_q),
    .in14(register_26_q), .in15(register_30_q), .in16(register_3_q), .in17(register_7_q),
    .in18(register_11_q), .in19(register_15_q), .in20(register_19_q), .in21(register_23_q),
    .in22(register_27_q), .in23(register_31_q), .in24(register_4_q), .in25(register_8_q),
    .in26(register_12_q), .in27(register_16_q), .in28(register_20_q), .in29(register_24_q),
    .in30(register_28_q), .in31(register_32_q), .out(RD1), .sel(A1));  // open: en
  Register #(.width(32)) register_5 (.D(in1), .en(WE), .Q(register_5_q), .clk(clk), .clr(reset));
  Register #(.width(32)) register_6 (.D(in9), .en(WE), .Q(register_6_q), .clk(clk), .clr(reset));
  Register #(.width(32)) register_7 (.D(in17), .en(WE), .Q(register_7_q), .clk(clk), .clr(reset));
  Register #(.width(32)) register_8 (.D(in25), .en(WE), .Q(register_8_q), .clk(clk), .clr(reset));
  Register #(.width(32)) register_9 (.D(in2), .en(WE), .Q(register_9_q), .clk(clk), .clr(reset));
  Register #(.width(32)) register_10 (.D(in10), .en(WE), .Q(register_10_q), .clk(clk), .clr(reset));
  Register #(.width(32)) register_11 (.D(in18), .en(WE), .Q(register_11_q), .clk(clk), .clr(reset));
  Register #(.width(32)) register_12 (.D(in26), .en(WE), .Q(register_12_q), .clk(clk), .clr(reset));
  Register #(.width(32)) register_13 (.D(in3), .en(WE), .Q(register_13_q), .clk(clk), .clr(reset));
  Register #(.width(32)) register_14 (.D(in11), .en(WE), .Q(register_14_q), .clk(clk), .clr(reset));
  Register #(.width(32)) register_15 (.D(in19), .en(WE), .Q(register_15_q), .clk(clk), .clr(reset));
  Register #(.width(32)) register_16 (.D(in27), .en(WE), .Q(register_16_q), .clk(clk), .clr(reset));
  Register #(.width(32)) register_17 (.D(in4), .en(WE), .Q(register_17_q), .clk(clk), .clr(reset));
  Register #(.width(32)) register_18 (.D(in12), .en(WE), .Q(register_18_q), .clk(clk), .clr(reset));
  Register #(.width(32)) register_19 (.D(in20), .en(WE), .Q(register_19_q), .clk(clk), .clr(reset));
  Register #(.width(32)) register_20 (.D(in28), .en(WE), .Q(register_20_q), .clk(clk), .clr(reset));
  Register #(.width(32)) register_21 (.D(in5), .en(WE), .Q(register_21_q), .clk(clk), .clr(reset));
  Register #(.width(32)) register_22 (.D(in13), .en(WE), .Q(register_22_q), .clk(clk), .clr(reset));
  Register #(.width(32)) register_23 (.D(in21), .en(WE), .Q(register_23_q), .clk(clk), .clr(reset));
  Register #(.width(32)) register_24 (.D(in29), .en(WE), .Q(register_24_q), .clk(clk), .clr(reset));
  Register #(.width(32)) register_25 (.D(in6), .en(WE), .Q(register_25_q), .clk(clk), .clr(reset));
  Register #(.width(32)) register_26 (.D(in14), .en(WE), .Q(register_26_q), .clk(clk), .clr(reset));
  Register #(.width(32)) register_27 (.D(in22), .en(WE), .Q(register_27_q), .clk(clk), .clr(reset));
  Register #(.width(32)) register_28 (.D(in30), .en(WE), .Q(register_28_q), .clk(clk), .clr(reset));
  Register #(.width(32)) register_29 (.D(in7), .en(WE), .Q(register_29_q), .clk(clk), .clr(reset));
  Register #(.width(32)) register_30 (.D(in15), .en(WE), .Q(register_30_q), .clk(clk), .clr(reset));
  Register #(.width(32)) register_31 (.D(in23), .en(WE), .Q(register_31_q), .clk(clk), .clr(reset));
  Register #(.width(32)) register_32 (.D(in31), .en(WE), .Q(register_32_q), .clk(clk), .clr(reset));
  Multiplexer #(.select(5), .width(32)) multiplexer_2 (
    .in0(register_1_q), .in1(register_5_q), .in2(register_9_q), .in3(register_13_q), .in4(register_17_q),
    .in5(register_21_q), .in6(register_25_q), .in7(register_29_q), .in8(register_2_q), .in9(register_6_q),
    .in10(register_10_q), .in11(register_14_q), .in12(register_18_q), .in13(register_22_q),
    .in14(register_26_q), .in15(register_30_q), .in16(register_3_q), .in17(register_7_q),
    .in18(register_11_q), .in19(register_15_q), .in20(register_19_q), .in21(register_23_q),
    .in22(register_27_q), .in23(register_31_q), .in24(register_4_q), .in25(register_8_q),
    .in26(register_12_q), .in27(register_16_q), .in28(register_20_q), .in29(register_24_q),
    .in30(register_28_q), .in31(register_32_q), .out(RD2), .sel(A2));  // open: en
  Demultiplexer #(.select(5), .width(32), .tristate("true")) demultiplexer_1 (
    .out1(in1), .out2(in2), .out3(in3), .out4(in4), .out5(in5), .out6(in6), .out7(in7), .out8(in8),
    .out9(in9), .out10(in10), .out11(in11), .out12(in12), .out13(in13), .out14(in14), .out15(in15),
    .out16(in16), .out17(in17), .out18(in18), .out19(in19), .out20(in20), .out21(in21), .out22(in22),
    .out23(in23), .out24(in24), .out25(in25), .out26(in26), .out27(in27), .out28(in28), .out29(in29),
    .out30(in30), .out31(in31), .in(WD), .sel(A3));  // open: out0, en
endmodule

module EXT (
  input  [15:0] init_imm,
  input  ext_sign,
  output [31:0] Out
);

  wire [31:0] bit_extender_1_out, bit_extender_2_out;

  assign bit_extender_1_out = {{16{1'b0}}, init_imm};  // Bit_Extender bit_extender_1
  assign bit_extender_2_out = {{16{init_imm[15]}}, init_imm};  // Bit_Extender bit_extender_2
  Multiplexer #(.width(32)) multiplexer_1 (
    .in0(bit_extender_1_out), .in1(bit_extender_2_out), .out(Out), .sel(ext_sign));  // open: en
endmodule

module Controller (
  input  [5:0] Funct,
  input  [5:0] Opcode,
  output MemtoReg,
  output MemWrite,
  output Branch,
  output [2:0] ALU_op,
  output ALUSrc,
  output RegDst,
  output RegWrite,
  output Extop,
  output isByte
);

  wire add, and_1_out, and_2_out, and_3_out, and_4_out, beq, find, lb, lui, lw, not_1_out, not_2_out,
       not_3_out, not_4_out, not_5_out, not_6_out, not_7_out, not_8_out, not_9_out, not_10_out, not_11_out,
       not_12_out, or_2_out, ori, sb, sub, sw;
  wire [3:0] bitfinder_1_index;

  not not_1 (not_1_out, Funct[4]);
  not not_2 (not_2_out, Funct[5]);
  not not_3 (not_3_out, Funct[2]);
  not not_4 (not_4_out, Funct[3]);
  not not_5 (not_5_out, Funct[0]);
  not not_6 (not_6_out, Funct[1]);
  not not_7 (not_7_out, Opcode[5]);
  not not_8 (not_8_out, Opcode[3]);
  not not_9 (not_9_out, Opcode[4]);
  not not_10 (not_10_out, Opcode[1]);
  not not_11 (not_11_out, Opcode[2]);
  not not_12 (not_12_out, Opcode[0]);
  and and_1 (and_1_out, Funct[5], not_1_out, not_4_out, not_3_out, not_6_out, not_5_out);
  and and_2 (and_2_out, not_7_out, not_9_out, not_8_out, not_11_out, not_10_out, not_12_out);
  and and_3 (and_3_out, Funct[5], not_1_out, not_4_out, not_3_out, Funct[1], not_5_out);
  and and_4 (and_4_out, not_7_out, not_9_out, not_8_out, not_11_out, not_10_out, not_12_out);
  and and_5 (ori, not_7_out, not_9_out, Opcode[3], Opcode[2], not_10_out, Opcode[0]);
  and and_6 (lw, Opcode[5], not_9_out, not_8_out, not_11_out, Opcode[1], Opcode[0]);
  and and_7 (sw, Opcode[5], not_9_out, Opcode[3], not_11_out, Opcode[1], Opcode[0]);
  and and_8 (beq, not_7_out, not_9_out, not_8_out, Opcode[2], not_10_out, not_12_out);
  and and_9 (lui, not_7_out, not_9_out, Opcode[3], Opcode[2], Opcode[1], Opcode[0]);
  and and_10 (lb, Opcode[5], not_9_out, not_8_out, not_11_out, not_10_out, not_12_out);
  and and_11 (sb, Opcode[5], not_9_out, Opcode[3], not_11_out, not_10_out, not_12_out);
  and and_12 (add, and_1_out, and_2_out);
  and and_13 (sub, and_3_out, and_4_out);
  and and_14 (MemWrite, sw, sb, find);
  and and_15 (Branch, beq, find);
  or or_1 (ALUSrc, lw, ori, lui, sw, lb, sb);
  or or_2 (or_2_out, lui, add, sub, ori, lw, lb);
  or or_3 (Extop, lw, lb, sw, sb, beq);
  or or_4 (isByte, lb, sb);
  or or_5 (MemtoReg, lb, lw);
  or or_6 (RegDst, add, sub);
  and and_16 (RegWrite, or_2_out, find);
  BitFinder #(.width(9)) bitfinder_1 (
    .in({sb, lb, lui, beq, sw, lw, ori, sub, add}), .index(bitfinder_1_index), .found(find));
  Multiplexer #(.select(4), .width(3)) multiplexer_1 (
    .in0(3'b001), .in1(3'b000), .in2(3'b010), .in3(3'b001), .in4(3'b001), .in5(3'b000), .in6(3'b011),
    .in7(3'b001), .in8(3'b001), .out(ALU_op), .sel(bitfinder_1_index));  // open: in9, in10, in11, in12, in13, in14, in15, en
endmodule

module DM (
  input  [31:0] Addr,
  input  Memwrite,
  input  clk,
  input  reset,
  input  [31:0] Data,
  input  isByte,
  output [31:0] WD1
);

  wire [4:0] bit_extender_2_out, shifter_1_out;
  wire [7:0] multiplexer_2_out;
  wire [31:0] and_1_out, bit_extender_1_out, bit_extender_3_out, multiplexer_1_out, not_1_out, or_1_out,
       ram_1_data, shifter_2_out, shifter_3_out;

  assign bit_extender_1_out = {{24{1'b0}}, Data[7:0]};  // Bit_Extender bit_extender_1
  assign bit_extender_2_out = {{3{1'b0}}, Addr[1:0]};  // Bit_Extender bit_extender_2
  Shifter #(.width(5)) shifter_1 (.in(bit_extender_2_out), .\dist (3'b011), .out(shifter_1_out));
  Multiplexer #(.width(32)) multiplexer_1 (
    .in0(Data), .in1(or_1_out), .out(multiplexer_1_out), .sel(isByte));  // open: en
  assign or_1_out = and_1_out | shifter_2_out;  // OR_Gate or_1, 32 bits wide
  Shifter #(.width(32)) shifter_2 (.in(bit_extender_1_out), .\dist (shifter_1_out), .out(shifter_2_out));
  Shifter #(.width(32)) shifter_3 (.in(32'hff), .\dist (shifter_1_out), .out(shifter_3_out));
  RAM #(.addrWidth(24), .dataWidth(32), .bus("separate")) ram_1 (
    .addr(Addr[25:2]), .din(multiplexer_1_out), .data(ram_1_data), .str(Memwrite), .clk(clk), .clr(reset));  // open: sel, ld
  assign not_1_out = ~shifter_3_out;  // NOT_Gate not_1, 32 bits wide
  assign and_1_out = ram_1_data & not_1_out;  // AND_Gate and_1, 32 bits wide
  Multiplexer #(.select(2), .width(8)) multiplexer_2 (
    .in0(ram_1_data[7:0]), .in1(ram_1_data[15:8]), .in2(ram_1_data[23:16]), .in3(ram_1_data[31:24]),
    .out(multiplexer_2_out), .sel(Addr[1:0]));  // open: en
  assign bit_extender_3_out = {{24{1'b0}}, multiplexer_2_out};  // Bit_Extender bit_extender_3
  Multiplexer #(.width(32)) multiplexer_3 (
    .in0(ram_1_data), .in1(bit_extender_3_out), .out(WD1), .sel(isByte));  // open: en

  // Other names for the same wires on the sheet: isB = isByte
endmodule
