// Logisim project Pre_Logisim_4BitSort.circ as structural Verilog: 4 circuits, main circuit 4bit_sort
module _4bit_sort (
  input  [3:0] A,
  input  [3:0] B,
  input  [3:0] C,
  input  [3:0] D,
  output [3:0] _1,
  output [3:0] _2,
  output [3:0] _3,
  output [3:0] _4
);

  wire [3:0] swap_logic_1_o1, swap_logic_1_o2, swap_logic_2_o1, swap_logic_2_o2, swap_logic_3_o1,
       swap_logic_4_o1, swap_logic_4_o2, swap_logic_6_o1;

  swap_logic swap_logic_1 (.I1(A), .I2(B), .O1(swap_logic_1_o1), .O2(swap_logic_1_o2));
  swap_logic swap_logic_2 (.I1(swap_logic_1_o2), .I2(C), .O1(swap_logic_2_o1), .O2(swap_logic_2_o2));
  swap_logic swap_logic_3 (.I1(swap_logic_2_o2), .I2(D), .O1(swap_logic_3_o1), .O2(_4));
  swap_logic swap_logic_4 (.I1(swap_logic_1_o1), .I2(swap_logic_2_o1), .O1(swap_logic_4_o1), .O2(swap_logic_4_o2));
  swap_logic swap_logic_5 (.I1(swap_logic_4_o1), .I2(swap_logic_6_o1), .O1(_1), .O2(_2));
  swap_logic swap_logic_6 (.I1(swap_logic_4_o2), .I2(swap_logic_3_o1), .O1(swap_logic_6_o1), .O2(_3));
endmodule

module _4bit_swap (
  input  [3:0] I1,
  input  [3:0] I2,
  input  En,
  output [3:0] O1,
  output [3:0] O2
);

  _1bit_swap u_1bit_swap_1 (.I11(I1[0]), .I22(I2[0]), .S(En), .O11(O1[0]), .O22(O2[0]));
  _1bit_swap u_1bit_swap_2 (.I11(I1[1]), .I22(I2[1]), .S(En), .O11(O1[1]), .O22(O2[1]));
  _1bit_swap u_1bit_swap_3 (.I11(I1[2]), .I22(I2[2]), .S(En), .O11(O1[2]), .O22(O2[2]));
  _1bit_swap u_1bit_swap_4 (.I11(I1[3]), .I22(I2[3]), .S(En), .O11(O1[3]), .O22(O2[3]));

  // Other names for the same wires on the sheet: I1_0 = I1[0]; I1_1 = I1[1]; I1_2 = I1[2]; I1_3 = I1[3]; I2_0 = I2[0];
  //   I2_1 = I2[1]; I2_2 = I2[2]; I2_3 = I2[3]; O1_0 = O1[0]; O1_1 = O1[1]; O1_2 = O1[2]; O1_3 = O1[3]; O2_0 = O2[0];
  //   O2_1 = O2[1]; O2_2 = O2[2]; O2_3 = O2[3]
endmodule

module _1bit_swap (
  input  I11,
  input  I22,
  input  S,
  output O11,
  output O22
);

  wire and_1_out, and_2_out, and_3_out, and_4_out, not_1_out;

  not not_1 (not_1_out, S);
  and and_1 (and_1_out, I11, not_1_out);
  and and_2 (and_2_out, I22, S);
  and and_3 (and_3_out, I11, S);
  and and_4 (and_4_out, I22, not_1_out);
  or or_1 (O11, and_1_out, and_2_out);
  or or_2 (O22, and_3_out, and_4_out);
endmodule

module swap_logic (
  input  [3:0] I1,
  input  [3:0] I2,
  output [3:0] O1,
  output [3:0] O2
);

  wire comparator_1_gt;

  Comparator #(.width(4), .mode("unsigned")) comparator_1 (.a(I1), .b(I2), .gt(comparator_1_gt));  // open: eq, lt
  _4bit_swap u_4bit_swap_1 (.I1(I1), .I2(I2), .En(comparator_1_gt), .O1(O1), .O2(O2));
endmodule
