// Logisim project Pre_Logisim_fibonacci_1.circ as structural Verilog: 3 circuits, main circuit main
module main (
  input  [2:0] \input ,
  output [3:0] out_2
);

  wire output_signal;
  wire [3:0] fib_now;

  // Probe on \input 
  fib_count fib_count_1 (.\input (\input ), .out_2(output_signal));
  fib_calculate fib_calculate_1 (.in_1(output_signal), .out_2(fib_now));
  Multiplexer #(.width(4)) multiplexer_1 (.in0(4'b0000), .in1(fib_now), .out(out_2), .sel(output_signal));  // open: en
endmodule

module fib_count (
  input  [2:0] \input ,
  output out_2
);

  wire click, undriven;
  wire [3:0] counter_value, max_value;

  Clock clock_1 (.out(click));
  assign max_value = {{1{1'b0}}, \input };  // Bit_Extender bit_extender_1
  Counter #(.width(4), .max('hf), .ongoal("stay")) counter_1 (
    .Q(counter_value), .clk(click), .clr(undriven));  // open: load, D, count, carry
  // Probe on max_value
  // Probe on counter_value
  Comparator #(.width(4), .mode("unsigned")) comparator_1 (
    .a(max_value), .b(counter_value), .lt(out_2));  // open: gt, eq
endmodule

module fib_calculate (
  input  in_1,
  output [3:0] out_2
);

  wire click, enable, initialize;
  wire [3:0] adder_1_out, multiplexer_1_out, prev;

  Clock clock_1 (.out(click));
  Counter #(.width(1), .max('h1), .ongoal("stay")) counter_1 (
    .Q(initialize), .clk(click));  // open: load, D, count, carry, clr
  not not_1 (enable, in_1);
  Multiplexer #(.width(4)) multiplexer_1 (
    .in0(4'b0001), .in1(out_2), .out(multiplexer_1_out), .sel(initialize));  // open: en
  Adder #(.width(4)) adder_1 (.a(prev), .b(out_2), .out(adder_1_out));  // open: cin, cout
  Register #(.width(4)) register_1 (.D(multiplexer_1_out), .en(enable), .Q(prev), .clk(click));  // open: clr
  Register #(.width(4)) register_2 (.D(adder_1_out), .en(enable), .Q(out_2), .clk(click));  // open: clr

  // Other names for the same wires on the sheet: now[3:0] = out_2
endmodule
