// Logisim project Pre_Logisim_fibonacci_2_DEBUG.circ as structural Verilog: 8 circuits, main circuit main
module main (
  input  [31:0] in_1,
  output [31:0] out_2
);

  wire freeze, n_Low;

  // Probe on in_1
  // Probe on in_1
  // Probe on n_Low
  // Probe on n_Low
  fib_count fib_count_1 (.in_1(in_1), .in_2(1'b0), .out_4(freeze), .out_3(n_Low));
  // Probe on freeze
  fib_calculate fib_calculate_1 (.in_1(n_Low), .in_2(freeze), .in_3(1'b0), .out_4(out_2));
  // Probe on out_2

  // Other names for the same wires on the sheet: input[31:0] = in_1
endmodule

module fib_count (
  input  [31:0] in_1,
  input  in_2,
  output out_3,
  output out_4
);

  wire clk, comparator_1_eq, init;
  wire [31:0] multiplexer_1_out, n, shifter_1_out;

  Counter #(.width(1), .max('h1), .ongoal("stay")) counter_1 (
    .Q(init), .clk(clk), .clr(in_2));  // open: load, D, count, carry
  Clock clock_1 (.out(clk));
  // Probe on in_1
  Multiplexer #(.width(32)) multiplexer_1 (
    .in0(in_1), .in1(shifter_1_out), .out(multiplexer_1_out), .sel(init));  // open: en
  Shifter #(.width(32), .shift("lr")) shifter_1 (.in(n), .\dist (5'b00001), .out(shifter_1_out));
  Comparator #(.width(32), .mode("unsigned")) comparator_1 (
    .a(n), .b({32{1'b0}}), .eq(comparator_1_eq));  // open: gt, lt
  // Probe on multiplexer_1_out
  Register #(.width(32)) register_1 (.D(multiplexer_1_out), .Q(n), .clk(clk), .clr(in_2));  // open: en
  Bit_Extender #(.in_width(32), .out_width(1)) bit_extender_1 (.in(n), .out(out_3));
  Multiplexer multiplexer_2 (.in0(1'b0), .in1(comparator_1_eq), .out(out_4), .sel(init));  // open: en
  // Probe on n

  // Other names for the same wires on the sheet: clr = in_2; input[31:0] = in_1
endmodule

module fib_calculate (
  input  in_1,
  input  in_2,
  input  in_3,
  output [31:0] out_4
);

  wire clk, ena, \initial ;
  wire [31:0] a11, a12, a21, a22, matrix_i_1_out_1, matrix_i_1_out_2, matrix_i_1_out_3, matrix_i_1_out_4,
       matrix_i_2_out_1, matrix_i_2_out_2, matrix_i_2_out_3, matrix_i_2_out_4, matrix_init_1_out_1,
       matrix_init_1_out_2, matrix_init_1_out_3, matrix_init_1_out_4, matrix_multiple_1_out_9,
       matrix_multiple_1_out_10, matrix_multiple_1_out_11, matrix_multiple_1_out_12, matrix_multiple_2_out_9,
       matrix_multiple_2_out_10, matrix_multiple_2_out_11, matrix_multiple_2_out_12, matrix_mux_1_out_10,
       matrix_mux_1_out_11, matrix_mux_1_out_12, matrix_mux_1_out_13, matrix_mux_2_out_10,
       matrix_mux_2_out_11, matrix_mux_2_out_12, matrix_mux_2_out_13, matrix_mux_3_out_10,
       matrix_mux_3_out_11, matrix_mux_3_out_12, matrix_mux_3_out_13, s11, s12, s21, s22;

  Counter #(.width(1), .max('h1), .ongoal("stay")) counter_1 (
    .Q(\initial ), .clk(clk), .clr(in_3));  // open: load, D, count, carry
  Clock clock_1 (.out(clk));
  // Probe on a11
  // Probe on a11
  matrix_I matrix_i_1 (
    .out_1(matrix_i_1_out_1), .out_2(matrix_i_1_out_2), .out_3(matrix_i_1_out_3), .out_4(matrix_i_1_out_4));
  // Probe on a11
  matrix_mux matrix_mux_1 (
    .in_1(matrix_i_1_out_1), .in_2(matrix_i_1_out_2), .in_3(matrix_i_1_out_3), .in_4(matrix_i_1_out_4),
    .in_5(a11), .in_6(a12), .in_7(a21), .in_8(a22), .in_9(in_1), .out_10(matrix_mux_1_out_10),
    .out_11(matrix_mux_1_out_11), .out_12(matrix_mux_1_out_12), .out_13(matrix_mux_1_out_13));
  // Probe on matrix_mux_2_out_10
  matrix_init matrix_init_1 (
    .out_1(matrix_init_1_out_1), .out_2(matrix_init_1_out_2), .out_3(matrix_init_1_out_3),
    .out_4(matrix_init_1_out_4));
  matrix_multiple matrix_multiple_1 (
    .in_1(a11), .in_2(a12), .in_3(a21), .in_4(a22), .in_5(a11), .in_6(a12), .in_7(a21), .in_8(a22),
    .out_9(matrix_multiple_1_out_9), .out_10(matrix_multiple_1_out_10), .out_11(matrix_multiple_1_out_11),
    .out_12(matrix_multiple_1_out_12));
  matrix_I matrix_i_2 (
    .out_1(matrix_i_2_out_1), .out_2(matrix_i_2_out_2), .out_3(matrix_i_2_out_3), .out_4(matrix_i_2_out_4));
  matrix_multiple matrix_multiple_2 (
    .in_1(s11), .in_2(s12), .in_3(s21), .in_4(s22), .in_5(matrix_mux_1_out_10), .in_6(matrix_mux_1_out_11),
    .in_7(matrix_mux_1_out_12), .in_8(matrix_mux_1_out_13), .out_9(matrix_multiple_2_out_9),
    .out_10(matrix_multiple_2_out_10), .out_11(matrix_multiple_2_out_11), .out_12(matrix_multiple_2_out_12));
  matrix_mux matrix_mux_2 (
    .in_1(matrix_init_1_out_1), .in_2(matrix_init_1_out_2), .in_3(matrix_init_1_out_3),
    .in_4(matrix_init_1_out_4), .in_5(matrix_multiple_1_out_9), .in_6(matrix_multiple_1_out_10),
    .in_7(matrix_multiple_1_out_11), .in_8(matrix_multiple_1_out_12), .in_9(\initial ),
    .out_10(matrix_mux_2_out_10), .out_11(matrix_mux_2_out_11), .out_12(matrix_mux_2_out_12),
    .out_13(matrix_mux_2_out_13));
  not not_1 (ena, in_2);
  // Probe on s12
  matrix_mux matrix_mux_3 (
    .in_1(matrix_i_2_out_1), .in_2(matrix_i_2_out_2), .in_3(matrix_i_2_out_3), .in_4(matrix_i_2_out_4),
    .in_5(matrix_multiple_2_out_9), .in_6(matrix_multiple_2_out_10), .in_7(matrix_multiple_2_out_11),
    .in_8(matrix_multiple_2_out_12), .in_9(\initial ), .out_10(matrix_mux_3_out_10),
    .out_11(matrix_mux_3_out_11), .out_12(matrix_mux_3_out_12), .out_13(matrix_mux_3_out_13));
  // Probe on a11
  matrix_register matrix_register_1 (
    .in_1(matrix_mux_2_out_10), .in_2(matrix_mux_2_out_11), .in_3(matrix_mux_2_out_12),
    .in_4(matrix_mux_2_out_13), .in_5(ena), .in_6(clk), .in_7(in_3), .out_8(a11), .out_9(a12), .out_10(a21),
    .out_11(a22));
  matrix_register matrix_register_2 (
    .in_1(matrix_mux_3_out_10), .in_2(matrix_mux_3_out_11), .in_3(matrix_mux_3_out_12),
    .in_4(matrix_mux_3_out_13), .in_5(ena), .in_6(clk), .in_7(in_3), .out_8(s11), .out_9(s12), .out_10(s21),
    .out_11(s22));
  Multiplexer #(.width(32)) multiplexer_1 (.in0({32{1'b0}}), .in1(s12), .out(out_4), .sel(in_2));  // open: en
  // Probe on s12

  // Other names for the same wires on the sheet: clr = in_3; freeze = in_2; n_Low = in_1
endmodule

module matrix_mux (
  input  [31:0] in_1,
  input  [31:0] in_2,
  input  [31:0] in_3,
  input  [31:0] in_4,
  input  [31:0] in_5,
  input  [31:0] in_6,
  input  [31:0] in_7,
  input  [31:0] in_8,
  input  in_9,
  output [31:0] out_10,
  output [31:0] out_11,
  output [31:0] out_12,
  output [31:0] out_13
);

  Multiplexer #(.width(32)) multiplexer_1 (.in0(in_1), .in1(in_5), .out(out_10), .sel(in_9));  // open: en
  Multiplexer #(.width(32)) multiplexer_2 (.in0(in_2), .in1(in_6), .out(out_11), .sel(in_9));  // open: en
  Multiplexer #(.width(32)) multiplexer_3 (.in0(in_3), .in1(in_7), .out(out_12), .sel(in_9));  // open: en
  Multiplexer #(.width(32)) multiplexer_4 (.in0(in_4), .in1(in_8), .out(out_13), .sel(in_9));  // open: en

  // Other names for the same wires on the sheet: a11[31:0] = in_1; a12[31:0] = in_2; a21[31:0] = in_3;
  //   a22[31:0] = in_4; b11[31:0] = in_5; b12[31:0] = in_6; b21[31:0] = in_7; b22[31:0] = in_8; select = in_9
endmodule

module matrix_init (
  output [31:0] out_1,
  output [31:0] out_2,
  output [31:0] out_3,
  output [31:0] out_4
);


  assign out_1 = 32'h1;
  assign out_2 = 32'h1;
  assign out_3 = 32'h1;
  assign out_4 = {32{1'b0}};
endmodule

module matrix_I (
  output [31:0] out_1,
  output [31:0] out_2,
  output [31:0] out_3,
  output [31:0] out_4
);


  assign out_1 = 32'h1;
  assign out_2 = {32{1'b0}};
  assign out_3 = {32{1'b0}};
  assign out_4 = 32'h1;
endmodule

module matrix_multiple (
  input  [31:0] in_1,
  input  [31:0] in_2,
  input  [31:0] in_3,
  input  [31:0] in_4,
  input  [31:0] in_5,
  input  [31:0] in_6,
  input  [31:0] in_7,
  input  [31:0] in_8,
  output [31:0] out_9,
  output [31:0] out_10,
  output [31:0] out_11,
  output [31:0] out_12
);

  wire [31:0] multiplier_1_cout, multiplier_1_out, multiplier_2_out, multiplier_3_cout, multiplier_3_out,
       multiplier_4_out, multiplier_5_cout, multiplier_5_out, multiplier_6_out, multiplier_7_cout,
       multiplier_7_out, multiplier_8_out;

  Multiplier #(.width(32)) multiplier_1 (
    .a(in_1), .b(in_5), .out(multiplier_1_out), .cout(multiplier_1_cout));  // open: cin
  Multiplier #(.width(32)) multiplier_2 (
    .a(in_2), .b(in_7), .out(multiplier_2_out), .cin(multiplier_1_cout));  // open: cout
  Multiplier #(.width(32)) multiplier_3 (
    .a(in_1), .b(in_6), .out(multiplier_3_out), .cout(multiplier_3_cout));  // open: cin
  Multiplier #(.width(32)) multiplier_4 (
    .a(in_2), .b(in_8), .out(multiplier_4_out), .cin(multiplier_3_cout));  // open: cout
  Multiplier #(.width(32)) multiplier_5 (
    .a(in_3), .b(in_5), .out(multiplier_5_out), .cout(multiplier_5_cout));  // open: cin
  Multiplier #(.width(32)) multiplier_6 (
    .a(in_4), .b(in_7), .out(multiplier_6_out), .cin(multiplier_5_cout));  // open: cout
  Multiplier #(.width(32)) multiplier_7 (
    .a(in_3), .b(in_6), .out(multiplier_7_out), .cout(multiplier_7_cout));  // open: cin
  Multiplier #(.width(32)) multiplier_8 (
    .a(in_4), .b(in_8), .out(multiplier_8_out), .cin(multiplier_7_cout));  // open: cout
  Adder #(.width(32)) adder_1 (.a(multiplier_1_out), .b(multiplier_2_out), .out(out_9));  // open: cin, cout
  Adder #(.width(32)) adder_2 (.a(multiplier_3_out), .b(multiplier_4_out), .out(out_10));  // open: cin, cout
  Adder #(.width(32)) adder_3 (.a(multiplier_5_out), .b(multiplier_6_out), .out(out_11));  // open: cin, cout
  Adder #(.width(32)) adder_4 (.a(multiplier_7_out), .b(multiplier_8_out), .out(out_12));  // open: cin, cout

  // Other names for the same wires on the sheet: a11[31:0] = in_1; a12[31:0] = in_2; a21[31:0] = in_3;
  //   a22[31:0] = in_4; b11[31:0] = in_5; b12[31:0] = in_6; b21[31:0] = in_7; b22[31:0] = in_8
endmodule

module matrix_register (
  input  [31:0] in_1,
  input  [31:0] in_2,
  input  [31:0] in_3,
  input  [31:0] in_4,
  input  in_5,
  input  in_6,
  input  in_7,
  output [31:0] out_8,
  output [31:0] out_9,
  output [31:0] out_10,
  output [31:0] out_11
);

  Register #(.width(32)) register_1 (.D(in_1), .en(in_5), .Q(out_8), .clk(in_6), .clr(in_7));
  Register #(.width(32)) register_2 (.D(in_2), .en(in_5), .Q(out_9), .clk(in_6), .clr(in_7));
  Register #(.width(32)) register_3 (.D(in_3), .en(in_5), .Q(out_10), .clk(in_6), .clr(in_7));
  Register #(.width(32)) register_4 (.D(in_4), .en(in_5), .Q(out_11), .clk(in_6), .clr(in_7));

  // Other names for the same wires on the sheet: a11_in[31:0] = in_1; a12_in[31:0] = in_2; a21_in[31:0] = in_3;
  //   a22_in[31:0] = in_4; clk = in_6; clr = in_7; enable = in_5
endmodule
